# Fritzing sketch Obstacle Detection Bot circuit (saved by Fritzing 0.9.3b)
breadboards: 1

parts:
  L298N1 = L298N DC motor driver
  Part2 = Arduino Uno (Rev3)
  M1 = DC Motor  # not connected
  M2 = DC Motor  # not connected
  Part3 = SRF05 Ultrasonic Rangefinder
  J2 = Basic Servo
  VCC1 = Battery block 9V

nets:
  N1: L298N1.IN1, Part2.D7
  N2: L298N1.IN2, Part2.D8
  N3: L298N1.IN3, Part2.D9_PWM
  N4: L298N1.IN4, Part2.D10_PWM/SS
  N5: Part2.D3_PWM, J2.pulse
  N6: Part2.D5_PWM, Part3.Trig
  N7: Part2.D6_PWM, Part3.Echo
  VCC: Part2.5V, Part3.VCC, J2.vcc
  GND: Part2.GND, Part3.GND, J2.gnd, VCC1.-

custom parts:
  L298N DC motor driver: 2x DC motor driver with 78M05 positive voltage regulator (7..35 V) L298N: max 46 V, 2 A Set 5 V Enable jumper to enable 5 V regultor (needed for the L298N) and +5 V output at screw terminal or supply external +5 V at screw terminal Set ENA and/or ENB to +5 V to enable motor permanently or supply ENA and/or ENB with PWM signal IN1 and IN2 set rotation directory for motor A (OUT1/OUT2) IN2 and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
